# Fritzing sketch mq7-schematics (saved by Fritzing 0.9.3b)
breadboards: 1

parts:
  Part1 = Arduino Nano (Rev3.0)
  R1 = Resistor [tolerance=±5% resistance=1k package=THT]
  LED1 = LED - 5mm [color="Green (565nm)" package="5 mm [THT]"]
  C1 = Tantalum Capacitor [capacitance=10µF package="100 mil [THT, tantalum]"]
  J1 = Piezo Speaker
  LED2 = LED - 5mm [color="Red (633nm)" package="5 mm [THT]"]
  Part2 = MQ-7 breakout
  R2 = Resistor [tolerance=±5% resistance=1k package=THT]
  Q1 = NPN-Transistor [package="TO92 [THT]"]
  R3 = Resistor [tolerance=±5% resistance=10k package=THT]
  C2 = Tantalum Capacitor [capacitance=10µF package="100 mil [THT, tantalum]"]

nets:
  N1: Part1.GND, Q1.E, R3.Pin_1
  N2: Part1.D3, R2.Pin_0
  N3: Part1.D5, J1.pin2
  N4: Part1.D6, J1.pin1
  N5: Part1.D9, LED1.cathode
  N6: Part1.D10, LED2.cathode
  5V: Part1.5V, R1.Pin_0, C1.+, Part2.VCC, C2.+
  N7: Part1.A1, C1.-, Part2.GND, Q1.C
  N8: Part1.A0, Part2.AO, R3.Pin_0, C2.-
  N9: R1.Pin_1, LED1.anode, LED2.anode
  N10: R2.Pin_1, Q1.B

custom parts:
  MQ-7 breakout: SKU: 101282
